// Digital circuit PC.dig as structural Verilog
module PC (
  input  [15:0] imm16,
  input  nPC_sel,
  input  En,
  input  CLK,
  output [31:0] OUT
);

  wire extender_1_p2, pulldown_2_out, pulldown_3_out;
  wire [15:0] barrelshifter_1_out;
  wire [31:0] add_1_s, add_2_s, extender_1_p3, multiplexer_1_out;

  BarrelShifter #(.Bits(16)) barrelshifter_1 (.in(imm16), .shift(5'b00010), .out(barrelshifter_1_out));
  // Extender extender_1: pin names not known; wires that end beside it: barrelshifter_1_out, extender_1_p2, extender_1_p3
  PullDown pulldown_1 (.out(extender_1_p2));
  PullDown pulldown_2 (.out(pulldown_2_out));
  PullDown pulldown_3 (.out(pulldown_3_out));
  Add #(.Bits(32)) add_1 (.a(OUT), .b(32'h4), .c_i(pulldown_2_out), .s(add_1_s));  // open: c_o
  Add #(.Bits(32)) add_2 (.a(add_1_s), .b(extender_1_p3), .c_i(pulldown_3_out), .s(add_2_s));  // open: c_o
  Multiplexer #(.Bits(32)) multiplexer_1 (.sel(nPC_sel), .in_0(add_1_s), .in_1(add_2_s), .out(multiplexer_1_out));
  Register #(.Bits(32)) register_1 (.D(multiplexer_1_out), .C(CLK), .en(En), .Q(OUT));
endmodule
